# Fritzing sketch Candy dispenser (saved by Fritzing 0.9.2b)
breadboards: 1

parts:
  S1 = Pushbutton [package="[THT]"]
  S2 = Pushbutton [package="[THT]"]
  S3 = Pushbutton [package="[THT]"]
  S4 = Pushbutton [package="[THT]"]
  S5 = Pushbutton [package="[THT]"]
  J1 = Piezo Speaker
  Часть2 = Arduino Nano (Rev3.0)
  R1 = Resistor [tolerance=±5% resistance=220 package="2512 [SMD]"]
  R2 = Resistor [tolerance=±5% resistance=220 package="2512 [SMD]"]
  R3 = Resistor [tolerance=±5% resistance=220 package="2512 [SMD]"]
  R4 = Resistor [tolerance=±5% resistance=220 package="2512 [SMD]"]
  R5 = Resistor [tolerance=±5% resistance=220 package="2512 [SMD]"]
  Nokia_5110_LCD_Module2 = Nokia5110LCDModule

nets:
  N1: S1.Pin_1, S1.Pin_2, S2.Pin_1, S2.Pin_2, S3.Pin_1, S3.Pin_2, S4.Pin_1, S4.Pin_2, S5.Pin_1, S5.Pin_2, J1.pin1, Часть2.GND, Nokia_5110_LCD_Module2.LED
  N2: S1.Pin_3, S1.Pin_4, Часть2.D6, R5.Pin_1
  N3: S2.Pin_3, S2.Pin_4, Часть2.D5, R4.Pin_1
  N4: S3.Pin_3, S3.Pin_4, Часть2.D2, R1.Pin_1
  N5: S4.Pin_3, S4.Pin_4, Часть2.D3, R2.Pin_1
  N6: S5.Pin_3, S5.Pin_4, Часть2.D4, R3.Pin_1
  N7: J1.pin2, Часть2.D12/MISO
  N8: Часть2.D7, Nokia_5110_LCD_Module2.Vcc
  N9: Часть2.D8, Nokia_5110_LCD_Module2.Grnd
  N10: Часть2.D9, Nokia_5110_LCD_Module2.SCE
  N11: Часть2.D10, Nokia_5110_LCD_Module2.RST
  N12: Часть2.D11/MOSI, Nokia_5110_LCD_Module2.D/C
  N13: Часть2.5V, R1.Pin_0, R2.Pin_0, R3.Pin_0, R4.Pin_0, R5.Pin_0, Nokia_5110_LCD_Module2.6_DN_(MOSI)

custom parts:
  : Nokia 5110 LCD with 8 pin. It's a 45mm*45mm module part. Description: The Nokia 5110 is a basic graphic LCD screen for lots of applications. It was originally intended for as a cell phone screen. This one is mounted on an easy to solder PCB. It uses the PCD8544 controller. The PCD8544 is a low power CMOS LCD controller/driver, designed to drive a graphic display of 48 rows and 84 columns. All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
